// Logisim project main.circ as structural Verilog: 17 circuits, main circuit Controller
module mips (
  input  reset
);

  wire clk;

  Clock clock_1 (.out(clk));
  DataPath datapath_1 ();  // open: clk, reset, sign, WeGrf, branch, WeDm, JType, jr, RegDst, WhichtoReg, AluSrc, AluOp, instr
  Controller controller_1 ();  // open: AluOp, WeDm, branch, AluSrc, sign, JType, instr, eq, A3DE, WDSelD, JReg, eqz, ltz

  // Notes on the sheet:
  //   MIPS
endmodule

module Controller (
  input  [31:0] instr,
  input  eq,
  input  eqz,
  input  ltz,
  output [4:0] A3DE,
  output WDSelD,
  output sign,
  output WeDm,
  output branch,
  output JType,
  output JReg,
  output [2:0] AluOp,
  output AluSrc
);

  wire addu, beq, j, jal, jalr, jr, lui, lw, not_1_out, not_2_out, not_3_out, not_4_out, not_5_out,
       not_6_out, not_7_out, not_8_out, not_9_out, not_10_out, not_11_out, not_12_out, ori, R, subu;
  wire [1:0] RegDst;

  // Probe on instr[31:26]
  not not_1 (not_1_out, instr[31]);
  not not_2 (not_2_out, instr[30]);
  not not_3 (not_3_out, instr[29]);
  not not_4 (not_4_out, instr[27]);
  not not_5 (not_5_out, instr[26]);
  not not_6 (not_6_out, instr[28]);
  // Probe on instr[5:0]
  not not_7 (not_7_out, instr[5]);
  not not_8 (not_8_out, instr[3]);
  not not_9 (not_9_out, instr[4]);
  not not_10 (not_10_out, instr[2]);
  not not_11 (not_11_out, instr[1]);
  not not_12 (not_12_out, instr[0]);
  and u_R (R, not_5_out, not_4_out, not_6_out, not_3_out, not_2_out, not_1_out);
  and u_addu (addu, R, instr[0], not_11_out, not_10_out, not_8_out, not_9_out, instr[5]);
  and u_subu (subu, R, instr[0], instr[1], not_10_out, not_8_out, not_9_out, instr[5]);
  and u_ori (ori, instr[26], not_4_out, instr[28], instr[29], not_2_out, not_1_out);
  and u_lw (lw, instr[26], instr[27], not_6_out, not_3_out, not_2_out, instr[31]);
  and sw (WeDm, instr[26], instr[27], not_6_out, instr[29], not_2_out, instr[31]);
  and u_beq (beq, not_5_out, not_4_out, instr[28], not_3_out, not_2_out, not_1_out);
  and u_lui (lui, instr[26], instr[27], instr[28], instr[29], not_2_out, not_1_out);
  and u_j (j, not_5_out, instr[27], not_6_out, not_3_out, not_2_out, not_1_out);
  and u_jal (jal, instr[26], instr[27], not_6_out, not_3_out, not_2_out, not_1_out);
  and u_jr (jr, R, not_12_out, not_11_out, not_10_out, instr[3], not_9_out, not_7_out);
  and u_jalr (jalr, R, instr[0], not_11_out, not_10_out, instr[3], not_9_out, not_7_out);
  or or_1 (AluSrc, ori, lw, WeDm, lui);
  or or_2 (RegDst[0], subu, addu, 1'b0, jalr, jal);
  or or_3 (RegDst[1], ori, lw, lui, jal);
  or or_4 (AluOp[0], subu, ori, 1'b0, 1'b0);
  buf or_5 (AluOp[1], ori);  // OR_Gate
  or or_6 (AluOp[2], lui, 1'b0);
  Multiplexer #(.select(2), .width(5), .enable("false")) multiplexer_1 (
    .in0({5{1'b0}}), .in1(instr[15:11]), .in2(instr[20:16]), .in3({5{1'b1}}), .out(A3DE), .sel(RegDst));
  // Probe on AluOp
  or or_7 (WDSelD, jal, jalr);
  and and_1 (branch, beq, eq);
  or or_8 (sign, lw, WeDm, beq);
  or or_9 (JType, j, jal);
  or or_10 (JReg, jr, jalr);

  // Other names for the same wires on the sheet: funct[5:0] = instr[5:0]; shamt[4:0] = instr[10:6];
  //   rd[4:0] = instr[15:11]; rt[4:0] = instr[20:16]; rs[4:0] = instr[25:21]; op[5:0] = instr[31:26]; sw = WeDm

  // Notes on the sheet:
  //   Controller
  //   addu subu lw sw lui ori beq j jal jr
  //   addu subu lw sw lui ori beq jal jr
  //   addu
  //   lw
  //   sw
  //   subu
  //   000+
  //   001-
  //   andi
  //   010&
  //   ori
  //   011|
  //   100 lui
  //   00 don't write
  //   01 rd is the WriteAddr
  //   10 rt is the WriteAddr
  //   11 31 is the WirteAddr
  //   0: reg, 1: ext(imm)
endmodule

module Forward (
  input  [4:0] RsD,
  input  [4:0] RtD,
  input  [4:0] RsE,
  input  [4:0] RtE,
  input  [4:0] RegWriteAddrE,
  input  WeGrfE,
  input  [4:0] RegWriteAddrM,
  input  WeGrfM,
  input  [4:0] RegWriteAddrW,
  input  WeGrfW,
  input  [4:0] RtM,
  output [1:0] FRD1D,
  output [1:0] FRD1E,
  output [1:0] FRD2D,
  output [1:0] FRD2E,
  output FRtM
);

  wire comparator_5_eq, comparator_6_eq, comparator_7_eq, RsD__GWAE, RsD__WRAM, RsD__WRAW, RsDtoE, RsDtoM,
       RsDtoW, RsE__WRAM, RsE__WRAW, RsEtoM, RsEtoW, RtD__GWAE, RtD__WRAM, RtD__WRAW, RtDtoE, RtDtoM, RtDtoW,
       RtE__WRAM, RtE__WRAW, RtEtoM, RtEtoW, RtM__RWAW, RWAE__0, RWAM__0, RWAW__0;

  Comparator #(.width(5), .mode("unsigned")) comparator_1 (.a(RtM), .b(RegWriteAddrW), .eq(RtM__RWAW));  // open: gt, lt
  Comparator #(.width(5), .mode("unsigned")) comparator_2 (.a(RsD), .b(RegWriteAddrE), .eq(RsD__GWAE));  // open: gt, lt
  Comparator #(.width(5), .mode("unsigned")) comparator_3 (.a(RsD), .b(RegWriteAddrM), .eq(RsD__WRAM));  // open: gt, lt
  Comparator #(.width(5), .mode("unsigned")) comparator_4 (.a(RsD), .b(RegWriteAddrW), .eq(RsD__WRAW));  // open: gt, lt
  Comparator #(.width(5), .mode("unsigned")) comparator_5 (
    .a(RegWriteAddrE), .b({5{1'b0}}), .eq(comparator_5_eq));  // open: gt, lt
  Comparator #(.width(5), .mode("unsigned")) comparator_6 (
    .a(RegWriteAddrM), .b({5{1'b0}}), .eq(comparator_6_eq));  // open: gt, lt
  Comparator #(.width(5), .mode("unsigned")) comparator_7 (
    .a(RegWriteAddrW), .b({5{1'b0}}), .eq(comparator_7_eq));  // open: gt, lt
  and and_1 (RsEtoM, WeGrfM, RWAM__0, RsE__WRAM);
  and and_2 (RsEtoW, WeGrfW, RWAW__0, RsE__WRAW);
  and and_3 (RtEtoM, WeGrfM, RWAM__0, RtE__WRAM);
  and and_4 (RtEtoW, WeGrfW, RWAW__0, RtE__WRAW);
  not not_1 (RWAE__0, comparator_5_eq);
  not not_2 (RWAM__0, comparator_6_eq);
  not not_3 (RWAW__0, comparator_7_eq);
  Comparator #(.width(5), .mode("unsigned")) comparator_8 (.a(RtD), .b(RegWriteAddrE), .eq(RtD__GWAE));  // open: gt, lt
  Comparator #(.width(5), .mode("unsigned")) comparator_9 (.a(RtD), .b(RegWriteAddrM), .eq(RtD__WRAM));  // open: gt, lt
  Comparator #(.width(5), .mode("unsigned")) comparator_10 (
    .a(RtD), .b(RegWriteAddrW), .eq(RtD__WRAW));  // open: gt, lt
  or or_1 (FRD1E[0], RsEtoM, 1'b0);
  or or_2 (FRD1E[1], RsEtoW, 1'b0);
  or or_3 (FRD2E[0], RtEtoM, 1'b0);
  or or_4 (FRD2E[1], RtEtoW, 1'b0);
  Comparator #(.width(5), .mode("unsigned")) comparator_11 (
    .a(RsE), .b(RegWriteAddrM), .eq(RsE__WRAM));  // open: gt, lt
  Comparator #(.width(5), .mode("unsigned")) comparator_12 (
    .a(RsE), .b(RegWriteAddrW), .eq(RsE__WRAW));  // open: gt, lt
  Comparator #(.width(5), .mode("unsigned")) comparator_13 (
    .a(RtE), .b(RegWriteAddrM), .eq(RtE__WRAM));  // open: gt, lt
  Comparator #(.width(5), .mode("unsigned")) comparator_14 (
    .a(RtE), .b(RegWriteAddrW), .eq(RtE__WRAW));  // open: gt, lt
  and and_5 (RsDtoE, WeGrfE, RWAE__0, RsD__GWAE);
  and and_6 (RsDtoM, WeGrfM, RWAM__0, RsD__WRAM);
  and and_7 (RsDtoW, WeGrfW, RWAW__0, RsD__WRAW);
  and and_8 (RtDtoE, WeGrfE, RWAE__0, RtD__GWAE);
  and and_9 (RtDtoM, WeGrfM, RWAM__0, RtD__WRAM);
  and and_10 (RtDtoW, WeGrfW, RWAW__0, RtD__WRAW);
  and and_11 (FRtM, RWAW__0, RtM__RWAW, WeGrfW);
  or or_5 (FRD1D[0], RsDtoE, RsDtoW);
  or or_6 (FRD1D[1], RsDtoM, RsDtoW);
  or or_7 (FRD2D[0], RtDtoE, RtDtoW);
  or or_8 (FRD2D[1], RtDtoM, RtDtoW);

  // Other names for the same wires on the sheet: RtMtoW = FRtM

  // Notes on the sheet:
  //   00 no F
  //   01 M comes
  //   10 W Comes
  //   00 no F
  //   01 M comes
  //   10 W Comes
  //   RdD1
  //   0 no F
  //   00 no F
  //   01 E comes
  //   10 M comes
  //   11 W Comes
  //   00 no F
  //   01 E comes
  //   10 M comes
  //   11 W Comes
  //   1 W comes
endmodule

module DataPath (
  input  clk,
  input  reset,
  input  WeGrf,
  input  WeDm,
  input  [1:0] RegDst,
  input  [1:0] WhichtoReg,
  input  AluSrc,
  input  [2:0] AluOp,
  input  sign,
  input  branch,
  input  JType,
  input  jr,
  output [31:0] instr
);

  wire AluSrcD, AluSrcE, EnPC, FRtM, undriven, undriven_2, WeDmD, WeDmE, WeDmM, WeDmW, WeGrfD, WeGrfE,
       WeGrfM, WeGrfW;
  wire [1:0] FRD1D, FRD1E, FRD2D, FRD2E, WhichtoRegD, WhichtoRegE, WhichtoRegM, WhichtoRegW;
  wire [2:0] AluOpD, AluOpE;
  wire [4:0] A3DE, A3W, RegWriteAddrE, RegWriteAddrM, RegWriteAddrW, RsD, RsE, RtD, RtE;
  wire [31:0] AluB, Fwd1D, Fwd2D, imm32DE, imm32E, InstrD, InstrE, InstrFD, InstrM, InstrW, MemReadM,
       MemReadW, multiplexer_1_out, multiplexer_2_out, multiplexer_4_out, NPC, PCD, PcD_t, PcE, PCF, PcM,
       PcW, RD1D, RD1DE, RD1E, RD2D, RD2DE, RD2E, RD2M, RegWrite, ResE, ResM, ResW, undriven_3, undriven_4,
       undriven_5, WDDE, WDW;

  PC pc_1 (.clk(clk), .reset(reset), .NPC(NPC), .PC(PCF), .en(EnPC));
  IM im_1 (.PC(PCF), .instr(InstrFD));
  IFID ifid_1 (.PcF(PCF), .InstrF(InstrFD), .PcD(PCD), .InstrD(InstrD));  // open: clk, en, reset
  Decode decode_1 (
    .clk(undriven), .reset(undriven_2), .PCF(PCF), .PCD(PCD), .InstrD(InstrD), .Fwd1D(Fwd1D), .Fwd2D(Fwd2D),
    .WDW(WDW), .A3W(A3W), .RD1DE(RD1DE), .RD2DE(RD2DE), .imm32DE(imm32DE), .A3DE(A3DE), .WDDE(WDDE));
  // IDEX idex_1: pin names not known; wires that end beside it: PcD_t, InstrD, RD1D, RD2D, WeGrfD, WeDmD, WhichtoRegD, AluSrcD, AluOpD, RsD, RtD, PcE, InstrE, RegWriteAddrE, RD1E, RD2E, imm32E, WeGrfE, WeDmE, WhichtoRegE, AluSrcE, AluOpE, RsE, RtE
  Multiplexer #(.select(2), .width(32), .enable("false")) multiplexer_1 (
    .in0(RD2E), .in1(ResM), .in2(RegWrite), .in3(undriven_3), .out(multiplexer_1_out), .sel(FRD2E));
  Multiplexer #(.select(2), .width(32), .enable("false")) multiplexer_2 (
    .in0(RD1E), .in1(ResM), .in2(RegWrite), .in3(undriven_4), .out(multiplexer_2_out), .sel(FRD1E));
  Multiplexer #(.width(32), .enable("false")) multiplexer_3 (
    .in0(multiplexer_1_out), .in1(imm32E), .out(AluB), .sel(AluSrcE));
  ALU alu_1 (.A(multiplexer_2_out), .B(AluB), .AluOp(AluOpE), .res(ResE));
  // Probe on ResE
  // Probe on AluOpE
  EXMEM exmem_1 (
    .PcE(PcE), .InstrE(InstrE), .RdE(RegWriteAddrE), .RD2E(RD2E), .ResE(ResE), .PcM(PcM), .InstrM(InstrM),
    .RdM(RegWriteAddrM), .RD2M(RD2M), .ResM(ResM), .WeGrfE(WeGrfE), .WhichtoRegE(WhichtoRegE), .WeDmE(WeDmE),
    .WhichtoRegM(WhichtoRegM), .WeGrfM(WeGrfM), .WeDmM(WeDmM));  // open: clk, en, reset
  Multiplexer #(.width(32), .enable("false")) multiplexer_4 (
    .in0(RD2M), .in1(RegWrite), .out(multiplexer_4_out), .sel(FRtM));
  DM dm_1 (.clk(clk), .reset(reset), .WD(multiplexer_4_out), .RD(MemReadM), .WE(WeDm), .MemAddr(ResM));
  Forward forward_1 (
    .RsD(RsD), .RtD(RtD), .RsE(RsE), .RtE(RtE), .RegWriteAddrE(RegWriteAddrE), .WeGrfE(WeGrfE),
    .RegWriteAddrM(RegWriteAddrM), .WeGrfM(WeGrfM), .RegWriteAddrW(RegWriteAddrW), .WeGrfW(WeGrfW),
    .FRD1D(FRD1D), .FRD1E(FRD1E), .FRD2D(FRD2D), .FRD2E(FRD2E), .RtM(InstrM[20:16]), .FRtM(FRtM));
  MEMWB memwb_1 (
    .PcM(PcM), .InstrM(InstrM), .RdM(RegWriteAddrM), .ResM(ResM), .MemReadM(MemReadM), .PcW(PcW),
    .InstrW(InstrW), .RdW(RegWriteAddrW), .ResW(ResW), .MemReadW(MemReadW), .WeGrfM(WeGrfM), .WeDmM(WeDmM),
    .WhichtoRegM(WhichtoRegM), .WeGrfW(WeGrfW), .WeDmW(WeDmW), .WhichtoRegW(WhichtoRegW));  // open: clk, en, reset
  Multiplexer #(.select(2), .width(32), .enable("false")) multiplexer_5 (
    .in0(ResW), .in1(MemReadW), .in2(undriven_5), .out(RegWrite), .sel(WhichtoRegW));  // open: in3
  // Probe on WhichtoRegW

  // Other names for the same wires on the sheet: RtM[4:0] = InstrM[20:16]

  // Notes on the sheet:
  //   Fetch
  //   IF/ID
  //   Datapath
  //   Decode
  //   EX
  //   000+
  //   001-
  //   010&
  //   011|
  //   MEM
  //   WB
endmodule

module Decode (
  input  clk,
  input  reset,
  input  [31:0] PCF,
  input  [31:0] PCD,
  input  [31:0] InstrD,
  input  [31:0] Fwd1D,
  input  [31:0] Fwd2D,
  input  [4:0] A3W,
  input  [31:0] WDW,
  output [31:0] RD1DE,
  output [31:0] RD2DE,
  output [31:0] imm32DE,
  output [4:0] A3DE,
  output [31:0] WDDE
);

  wire branch, eq, JReg, JType, sign, WDSelD;
  wire [31:0] NPC, PCD8;

  EXT ext_1 (.imm16(InstrD[15:0]), .imm32(imm32DE), .sign(sign));
  Controller controller_1 (
    .branch(branch), .sign(sign), .JType(JType), .instr(InstrD), .eq(eq), .A3DE(A3DE), .WDSelD(WDSelD),
    .JReg(JReg));  // open: AluOp, WeDm, AluSrc, eqz, ltz
  NPC npc_1 (
    .branch(branch), .JType(JType), .jr(JReg), .PC(PCF), .RegJump(Fwd1D), .imm26(InstrD[25:0]), .NPC(NPC),
    .PcD(PCD));
  GRF grf_1 (
    .A1(InstrD[25:21]), .A2(InstrD[20:16]), .A3(A3W), .WD(WDW), .RD1(RD1DE), .RD2(RD2DE), .clk(clk),
    .reset(reset));
  Comparator #(.width(32)) comparator_1 (.a(Fwd1D), .b(Fwd2D), .eq(eq));  // open: gt, lt
  Adder #(.width(32)) adder_1 (.a(PCD), .b(32'h8), .out(PCD8));  // open: cin, cout
  Multiplexer #(.width(32), .enable("false")) multiplexer_1 (.in0({32{1'b0}}), .in1(PCD8), .out(WDDE), .sel(WDSelD));

  // Other names for the same wires on the sheet: funct[5:0] = InstrD[5:0]; imm26D[25:0] = InstrD[25:0];
  //   shamt[4:0] = InstrD[10:6]; rd[4:0] = InstrD[15:11]; rt[4:0] = InstrD[20:16]; rs[4:0] = InstrD[25:21];
  //   op[5:0] = InstrD[31:26]

  // Notes on the sheet:
  //   Decode
endmodule

module EXT (
  input  [15:0] imm16,
  input  sign,
  output [31:0] imm32
);

  wire [31:0] bit_extender_1_out, bit_extender_2_out;

  assign bit_extender_1_out = {{16{1'b0}}, imm16};  // Bit_Extender bit_extender_1
  assign bit_extender_2_out = {{16{imm16[15]}}, imm16};  // Bit_Extender bit_extender_2
  Multiplexer #(.width(32), .enable("false")) multiplexer_1 (
    .in0(bit_extender_1_out), .in1(bit_extender_2_out), .out(imm32), .sel(sign));
endmodule

module GRF (
  input  clk,
  input  reset,
  input  [4:0] A1,
  input  [4:0] A2,
  input  [4:0] A3,
  input  [31:0] WD,
  output [31:0] RD1,
  output [31:0] RD2
);

  wire A1__A3, A2__A3, undriven, undriven_2, undriven_3, undriven_4, undriven_5, undriven_6, undriven_7,
       undriven_8, undriven_9, undriven_10, undriven_11, undriven_12, undriven_13, undriven_14, undriven_15,
       undriven_16, undriven_17, undriven_18, undriven_19, undriven_20, undriven_21, undriven_22,
       undriven_23, undriven_24, undriven_25, undriven_26, undriven_27;
  wire [31:0] in00, in01, in02, in03, in04, in05, in06, in07, in08, in09, in10, in11, in12, in13, in14, in15,
       in16, in17, in18, in19, in20, in21, in22, in23, in24, in25, in26, in27, in28, in29, in30, in31, out00,
       out01, out02, out03, out04, out05, out06, out07, out08, out09, out10, out11, out12, out13, out14,
       out15, out16, out17, out18, out19, out20, out21, out22, out23, out24, out25, out26, out27, out28,
       out29, out30, out31, RD1_t, RD2_t;

  // Probe on WD
  Demultiplexer #(.select(5), .width(32), .tristate("true"), .enable("false")) demultiplexer_1 (
    .out0(in00), .out1(in01), .out2(in02), .out3(in03), .out4(in04), .out5(in05), .out6(in06), .out7(in07),
    .out8(in08), .out9(in09), .out10(in10), .out11(in11), .out12(in12), .out13(in13), .out14(in14),
    .out15(in15), .out16(in16), .out17(in17), .out18(in18), .out19(in19), .out20(in20), .out21(in21),
    .out22(in22), .out23(in23), .out24(in24), .out25(in25), .out26(in26), .out27(in27), .out28(in28),
    .out29(in29), .out30(in30), .out31(in31), .in(WD), .sel(A3));
  // Probe on A3
  Register #(.width(32)) register_1 (.D(in00), .Q(out00), .clr(1'b1));  // open: en, clk
  Register #(.width(32)) register_2 (.D(in08), .en(undriven), .Q(out08), .clk(clk), .clr(reset));
  Register #(.width(32)) register_3 (.D(in16), .en(undriven_2), .Q(out16), .clk(clk), .clr(reset));
  Register #(.width(32)) register_4 (.D(in24), .en(undriven_3), .Q(out24), .clk(clk), .clr(reset));
  Register #(.width(32)) register_5 (.D(in01), .Q(out01), .clk(clk), .clr(reset));  // open: en
  Register #(.width(32)) register_6 (.D(in09), .en(undriven_4), .Q(out09), .clk(clk), .clr(reset));
  Register #(.width(32)) register_7 (.D(in17), .en(undriven_5), .Q(out17), .clk(clk), .clr(reset));
  Register #(.width(32)) register_8 (.D(in25), .en(undriven_6), .Q(out25), .clk(clk), .clr(reset));
  Comparator #(.width(5)) comparator_1 (.a(A3), .b(A1), .eq(A1__A3));  // open: gt, lt
  Comparator #(.width(5)) comparator_2 (.a(A3), .b(A2), .eq(A2__A3));  // open: gt, lt
  Multiplexer #(.select(5), .width(32), .enable("false")) multiplexer_1 (
    .in0(out00), .in1(out01), .in2(out02), .in3(out03), .in4(out04), .in5(out05), .in6(out06), .in7(out07),
    .in8(out08), .in9(out09), .in10(out10), .in11(out11), .in12(out12), .in13(out13), .in14(out14),
    .in15(out15), .in16(out16), .in17(out17), .in18(out18), .in19(out19), .in20(out20), .in21(out21),
    .in22(out22), .in23(out23), .in24(out24), .in25(out25), .in26(out26), .in27(out27), .in28(out28),
    .in29(out29), .in30(out30), .in31(out31), .out(RD1_t), .sel(A1));
  Register #(.width(32)) register_9 (.D(in02), .Q(out02), .clk(clk), .clr(reset));  // open: en
  Register #(.width(32)) register_10 (.D(in10), .en(undriven_7), .Q(out10), .clk(clk), .clr(reset));
  Register #(.width(32)) register_11 (.D(in18), .en(undriven_8), .Q(out18), .clk(clk), .clr(reset));
  Register #(.width(32)) register_12 (.D(in26), .en(undriven_9), .Q(out26), .clk(clk), .clr(reset));
  Multiplexer #(.width(32), .enable("false")) multiplexer_2 (.in0(RD1_t), .in1(WD), .out(RD1), .sel(A1__A3));
  Multiplexer #(.width(32), .enable("false")) multiplexer_3 (.in0(RD2_t), .in1(WD), .out(RD2), .sel(A2__A3));
  Register #(.width(32)) register_13 (.D(in03), .Q(out03), .clk(clk), .clr(reset));  // open: en
  Register #(.width(32)) register_14 (.D(in11), .en(undriven_10), .Q(out11), .clk(clk), .clr(reset));
  Register #(.width(32)) register_15 (.D(in19), .en(undriven_11), .Q(out19), .clk(clk), .clr(reset));
  Register #(.width(32)) register_16 (.D(in27), .en(undriven_12), .Q(out27), .clk(clk), .clr(reset));
  Register #(.width(32)) register_17 (.D(in04), .en(undriven_13), .Q(out04), .clk(clk), .clr(reset));
  Register #(.width(32)) register_18 (.D(in12), .en(undriven_14), .Q(out12), .clk(clk), .clr(reset));
  Register #(.width(32)) register_19 (.D(in20), .en(undriven_15), .Q(out20), .clk(clk), .clr(reset));
  Register #(.width(32)) register_20 (.D(in28), .en(undriven_16), .Q(out28), .clk(clk), .clr(reset));
  Multiplexer #(.select(5), .width(32), .enable("false")) multiplexer_4 (
    .in0(out00), .in1(out01), .in2(out02), .in3(out03), .in4(out04), .in5(out05), .in6(out06), .in7(out07),
    .in8(out08), .in9(out09), .in10(out10), .in11(out11), .in12(out12), .in13(out13), .in14(out14),
    .in15(out15), .in16(out16), .in17(out17), .in18(out18), .in19(out19), .in20(out20), .in21(out21),
    .in22(out22), .in23(out23), .in24(out24), .in25(out25), .in26(out26), .in27(out27), .in28(out28),
    .in29(out29), .in30(out30), .in31(out31), .out(RD2_t), .sel(A2));
  Register #(.width(32)) register_21 (.D(in05), .Q(out05), .clk(clk), .clr(reset));  // open: en
  Register #(.width(32)) register_22 (.D(in13), .en(undriven_17), .Q(out13), .clk(clk), .clr(reset));
  Register #(.width(32)) register_23 (.D(in21), .en(undriven_18), .Q(out21), .clk(clk), .clr(reset));
  Register #(.width(32)) register_24 (.D(in29), .en(undriven_19), .Q(out29), .clk(clk), .clr(reset));
  Register #(.width(32)) register_25 (.D(in06), .en(undriven_20), .Q(out06), .clk(clk), .clr(reset));
  Register #(.width(32)) register_26 (.D(in14), .en(undriven_21), .Q(out14), .clk(clk), .clr(reset));
  Register #(.width(32)) register_27 (.D(in22), .en(undriven_22), .Q(out22), .clk(clk), .clr(reset));
  Register #(.width(32)) register_28 (.D(in30), .en(undriven_23), .Q(out30), .clk(clk), .clr(reset));
  Register #(.width(32)) register_29 (.D(in07), .en(undriven_24), .Q(out07), .clk(clk), .clr(reset));
  Register #(.width(32)) register_30 (.D(in15), .en(undriven_25), .Q(out15), .clk(clk), .clr(reset));
  Register #(.width(32)) register_31 (.D(in23), .en(undriven_26), .Q(out23), .clk(clk), .clr(reset));
  Register #(.width(32)) register_32 (.D(in31), .en(undriven_27), .Q(out31), .clk(clk), .clr(reset));

  // Notes on the sheet:
  //   Global Register File
endmodule

module NPC (
  input  branch,
  input  JType,
  input  jr,
  input  [31:0] PC,
  input  [31:0] PcD,
  input  [31:0] RegJump,
  input  [25:0] imm26,
  output [31:0] NPC
);

  wire [31:0] bit_extender_1_out, multiplexer_1_out, multiplexer_2_out, PC4, PcBranch, PcD4, shifter_1_out;

  // Probe on PC
  // Probe on PcD
  Multiplexer #(.width(32), .enable("false")) multiplexer_1 (
    .in0(PC4), .in1(PcBranch), .out(multiplexer_1_out), .sel(branch));
  assign bit_extender_1_out = {{16{imm26[15]}}, imm26[15:0]};  // Bit_Extender bit_extender_1
  Adder #(.width(32)) adder_1 (.a(PC), .b(32'h4), .out(PC4));  // open: cin, cout
  Adder #(.width(32)) adder_2 (.a(PcD), .b(32'h4), .out(PcD4));  // open: cin, cout
  Shifter #(.width(32)) shifter_1 (.in(bit_extender_1_out), .\dist (5'b00010), .out(shifter_1_out));
  Multiplexer #(.width(32), .enable("false")) multiplexer_2 (
    .in0(multiplexer_1_out), .in1({PcD4[31:28], imm26, 2'b00}), .out(multiplexer_2_out), .sel(JType));
  Adder #(.width(32)) adder_3 (.a(shifter_1_out), .b(PcD4), .out(PcBranch));  // open: cin, cout
  // Probe on NPC
  Multiplexer #(.width(32), .enable("false")) multiplexer_3 (
    .in0(multiplexer_2_out), .in1(RegJump), .out(NPC), .sel(jr));

  // Other names for the same wires on the sheet: PcJ[31:2] = {PcD4[31:28], imm26}; PcJr[31:0] = RegJump

  // Notes on the sheet:
  //   NPC
endmodule

module PC (
  input  clk,
  input  reset,
  input  en,
  input  [31:0] NPC,
  output [31:0] PC
);

  wire comparator_1_eq;
  wire [31:0] multiplexer_1_out, PC_q;

  // Probe on NPC
  Multiplexer #(.width(32), .enable("false")) multiplexer_1 (
    .in0(NPC), .in1(32'h3000), .out(multiplexer_1_out), .sel(reset));
  Register #(.width(32)) u_PC (.D(multiplexer_1_out), .en(en), .Q(PC_q), .clk(clk));  // open: clr
  Comparator #(.width(32)) comparator_1 (.a(PC_q), .b({32{1'b0}}), .eq(comparator_1_eq));  // open: gt, lt
  Multiplexer #(.width(32), .enable("false")) multiplexer_2 (
    .in0(PC_q), .in1(32'h3000), .out(PC), .sel(comparator_1_eq));
endmodule

module IM (
  input  [31:0] PC,
  output [31:0] instr
);

  wire [31:0] subtractor_1_out;

  Subtractor #(.width(32)) subtractor_1 (.a(PC), .b(32'h3000), .out(subtractor_1_out));  // open: bin, bout
  ROM #(.addrWidth(10), .dataWidth(32)) rom_1 (.addr(subtractor_1_out[11:2]), .data(instr));  // open: sel

  // Notes on the sheet:
  //   IM
  //   contents of rom_1 (hex, n*v repeats v):
  //   34040100 34850123 3c0601c8 3c07ffff 34e7ffff 868021 878821 e7a021 869023 879823 ac040000 ac050004
  //   ac060008 ac07000c ac100010 ac110014 ac120018 ac13002c ac140030 8c040000 8c05000c ac04001c ac050020
  //   34040001 34050002 34060001 10850001 10860001 ad040024 ad050028 c000c23 c000c23 ad150040 34a50004
  //   c000c27 ad050038 ad1f003c 36b50005 3e00008 ad050044 ad1f0048
endmodule

module ALU (
  input  [31:0] A,
  input  [31:0] B,
  input  [2:0] AluOp,
  output [31:0] res
);

  wire [31:0] adder_1_out, and_1_out, or_1_out, subtractor_1_out;

  Adder #(.width(32)) adder_1 (.a(A), .b(B), .out(adder_1_out));  // open: cin, cout
  Subtractor #(.width(32)) subtractor_1 (.a(A), .b(B), .out(subtractor_1_out));  // open: bin, bout
  assign and_1_out = A & B;  // AND_Gate and_1, 32 bits wide
  assign or_1_out = A | B;  // OR_Gate or_1, 32 bits wide
  // Probe on A
  // Probe on B
  // Probe on res
  Multiplexer #(.select(3), .width(32), .enable("false")) multiplexer_1 (
    .in0(adder_1_out), .in1(subtractor_1_out), .in2(and_1_out), .in3(or_1_out), .in4({B[15:0], {16{1'b0}}}),
    .out(res), .sel(AluOp));  // open: in5, in6, in7

  // Notes on the sheet:
  //   Arithmetic and Logic Unit
  //   000+
  //   001-
  //   010&
  //   011|
  //   100 lui
endmodule

module DM (
  input  clk,
  input  reset,
  input  WE,
  input  [31:0] MemAddr,
  input  [31:0] WD,
  output [31:0] RD
);

  // Probe on MemAddr[11:2]
  // Probe on WD
  RAM #(.addrWidth(10), .dataWidth(32), .bus("separate")) ram_1 (
    .addr(MemAddr[11:2]), .din(WD), .data(RD), .str(WE), .clk(clk), .clr(reset));  // open: sel, ld

  // Notes on the sheet:
  //   but mips address by byte(8 bits)
  //   Data Memory
  //   addressing by word(32 bits)
endmodule

module IFID (
  input  clk,
  input  en,
  input  reset,
  input  [31:0] PcF,
  input  [31:0] InstrF,
  output [31:0] PcD,
  output [31:0] InstrD
);

  Register #(.width(32)) PC (.D(PcF), .en(en), .Q(PcD), .clk(clk), .clr(reset));
  Register #(.width(32)) PC_2 ();  // open: D, en, Q, clk, clr
  Register #(.width(32)) instr (.D(InstrF), .en(en), .Q(InstrD), .clk(clk), .clr(reset));

  // Notes on the sheet:
  //   IFID
endmodule

module IDEX (
  input  en,
  input  clk,
  input  reset,
  input  [4:0] RdD,
  input  [31:0] PcD,
  input  [31:0] InstrD,
  input  [31:0] RD1D,
  input  [31:0] RD2D,
  input  [31:0] imm32D,
  input  WeGrfD,
  input  WeDmD,
  input  [1:0] WhichtoRegD,
  input  AluSrcD,
  input  [2:0] AluOpD,
  input  [4:0] RsD,
  input  [4:0] RtD,
  output [4:0] RdE,
  output [31:0] PcE,
  output [31:0] InstrE,
  output [31:0] RD1E,
  output [31:0] RD2E,
  output [31:0] imm32E,
  output WeGrfE,
  output WeDmE,
  output [1:0] WhichtoRegE,
  output AluSrcE,
  output [2:0] AluOpE,
  output [4:0] RsE,
  output [4:0] RtE
);

  Register #(.width(32)) PC (.D(PcD), .en(en), .Q(PcE), .clk(clk), .clr(reset));
  Register #(.width(32)) RD1 (.D(RD1D), .en(en), .Q(RD1E), .clk(clk), .clr(reset));
  Register #(.width(32)) imm32 (.D(imm32D), .en(en), .Q(imm32E), .clk(clk), .clr(reset));
  Register #(.width(1)) WeGrf (.D(WeGrfD), .en(en), .Q(WeGrfE), .clk(clk), .clr(reset));
  Register #(.width(1)) AluSrc (.D(AluSrcD), .en(en), .Q(AluSrcE), .clk(clk), .clr(reset));
  Register #(.width(5)) Rs (.D(RsD), .en(en), .Q(RsE), .clk(clk), .clr(reset));
  Register #(.width(32)) PC_2 ();  // open: D, en, Q, clk, clr
  Register #(.width(32)) instr (.D(InstrD), .en(en), .Q(InstrE), .clk(clk), .clr(reset));
  Register #(.width(32)) RD2 (.D(RD2D), .en(en), .Q(RD2E), .clk(clk), .clr(reset));
  Register #(.width(1)) WeDm (.D(WeDmD), .en(en), .Q(WeDmE), .clk(clk), .clr(reset));
  Register #(.width(3)) AluOp (.D(AluOpD), .en(en), .Q(AluOpE), .clk(clk), .clr(reset));
  Register #(.width(5)) Rt (.D(RtD), .en(en), .Q(RtE), .clk(clk), .clr(reset));
  Register #(.width(5)) rd (.D(RdD), .en(en), .Q(RdE), .clk(clk), .clr(reset));
  Register #(.width(2)) WhichtoReg (.D(WhichtoRegD), .en(en), .Q(WhichtoRegE), .clk(clk), .clr(reset));

  // Notes on the sheet:
  //   IDEX
endmodule

module EXMEM (
  input  clk,
  input  en,
  input  reset,
  input  [31:0] PcE,
  input  [31:0] InstrE,
  input  [4:0] RdE,
  input  [31:0] RD2E,
  input  [31:0] ResE,
  input  WeGrfE,
  input  WeDmE,
  input  [1:0] WhichtoRegE,
  output [31:0] PcM,
  output [31:0] InstrM,
  output [4:0] RdM,
  output [31:0] RD2M,
  output [31:0] ResM,
  output WeGrfM,
  output WeDmM,
  output [1:0] WhichtoRegM
);

  Register #(.width(32)) PC (.D(PcE), .en(en), .Q(PcM), .clk(clk), .clr(reset));
  Register #(.width(32)) res (.D(ResE), .en(en), .Q(ResM), .clk(clk), .clr(reset));
  Register #(.width(32)) RD2 (.D(RD2E), .en(en), .Q(RD2M), .clk(clk), .clr(reset));
  Register #(.width(1)) WeGrf (.D(WeGrfE), .en(en), .Q(WeGrfM), .clk(clk), .clr(reset));
  Register #(.width(5)) rd (.D(RdE), .en(en), .Q(RdM), .clk(clk), .clr(reset));
  Register #(.width(1)) WeDm (.D(WeDmE), .en(en), .Q(WeDmM), .clk(clk), .clr(reset));
  Register #(.width(32)) PC_2 ();  // open: D, en, Q, clk, clr
  Register #(.width(32)) instr (.D(InstrE), .en(en), .Q(InstrM), .clk(clk), .clr(reset));
  Register #(.width(2)) WhichtoReg (.D(WhichtoRegE), .en(en), .Q(WhichtoRegM), .clk(clk), .clr(reset));

  // Notes on the sheet:
  //   EXMEM
endmodule

module MEMWB (
  input  clk,
  input  en,
  input  reset,
  input  [31:0] PcM,
  input  [31:0] InstrM,
  input  [4:0] RdM,
  input  [31:0] ResM,
  input  [31:0] MemReadM,
  input  WeGrfM,
  input  WeDmM,
  input  [1:0] WhichtoRegM,
  output [31:0] PcW,
  output [31:0] InstrW,
  output [4:0] RdW,
  output [31:0] ResW,
  output [31:0] MemReadW,
  output WeGrfW,
  output WeDmW,
  output [1:0] WhichtoRegW
);

  Register #(.width(32)) PC (.D(PcM), .en(en), .Q(PcW), .clk(clk), .clr(reset));
  Register #(.width(32)) res (.D(ResM), .en(en), .Q(ResW), .clk(clk), .clr(reset));
  Register #(.width(1)) WeGrf (.D(WeGrfM), .en(en), .Q(WeGrfW), .clk(clk), .clr(reset));
  Register #(.width(32)) MemRead (.D(MemReadM), .en(en), .Q(MemReadW), .clk(clk), .clr(reset));
  Register #(.width(5)) rd (.D(RdM), .en(en), .Q(RdW), .clk(clk), .clr(reset));
  Register #(.width(32)) PC_2 ();  // open: D, en, Q, clk, clr
  Register #(.width(32)) instr (.D(InstrM), .en(en), .Q(InstrW), .clk(clk), .clr(reset));
  Register #(.width(1)) WeDm (.D(WeDmM), .en(en), .Q(WeDmW), .clk(clk), .clr(reset));
  Register #(.width(2)) WhichtoReg (.D(WhichtoRegM), .en(en), .Q(WhichtoRegW), .clk(clk), .clr(reset));

  // Notes on the sheet:
  //   MEMWB
endmodule

module test (
);

  Controller controller_1 ();  // open: AluOp, WeDm, branch, AluSrc, sign, JType, instr, eq, A3DE, WDSelD, JReg, eqz, ltz
endmodule
